# Fritzing sketch 2025 Data Schematic (saved by Fritzing 1.0.2b)

parts:
  CANivore1 = CTRE CANivore [form="♀ (female)" package=THT]
  Kraken3 = Kraken- Left1
  Kraken4 = Kraken- Left1
  Kraken5 = Kraken- Left1
  Kraken6 = Kraken- Left1
  Pigeon_2_1 = CTRE Pigeon 2.0 [package=THT]
  cntl1 = roborio_v2
  switch4 = Network Switch
  J2 = Generic female header - 5 pins [form="♀ (female)" package=THT]
  RSL1 = FRC Robot Signal Light [part_number=855PB-B12ME522]
  J3 = Generic female header - 1 pins [form="♀ (female)" package=THT]
  J4 = Generic female header - 1 pins [form="♀ (female)" package=THT]
  RGB_Strip_LED17 = RGB Strip LED  # not connected
  RGB_Strip_LED18 = RGB Strip LED  # not connected
  RGB_Strip_LED19 = RGB Strip LED  # not connected
  RGB_Strip_LED20 = RGB Strip LED  # not connected
  RGB_Strip_LED22 = RGB Strip LED  # not connected
  RGB_Strip_LED23 = RGB Strip LED  # not connected
  RGB_Strip_LED24 = RGB Strip LED  # not connected
  RGB_Strip_LED25 = RGB Strip LED  # not connected
  RGB_Strip_LED26 = RGB Strip LED  # not connected
  RGB_Strip_LED27 = RGB Strip LED  # not connected
  RGB_Strip_LED28 = RGB Strip LED  # not connected
  RGB_Strip_LED29 = RGB Strip LED  # not connected
  RGB_Strip_LED30 = RGB Strip LED
  RGB_Strip_LED32 = RGB Strip LED  # not connected
  CANcoder3 = CTRE CANcoder [package=THT]
  CANcoder4 = CTRE CANcoder [package=THT]
  CANcoder7 = CTRE CANcoder [package=THT]
  CANcoder8 = CTRE CANcoder [package=THT]
  Kraken15 = Kraken- Left1
  Kraken16 = Kraken- Left1
  Kraken17 = Kraken- Left1
  Kraken18 = Kraken- Left1
  Kraken19 = Kraken- Left1
  Kraken20 = Kraken- Left1
  CANcoder9 = CTRE CANcoder [package=THT]
  CANcoder10 = CTRE CANcoder [package=THT]
  Kraken22 = Kraken- Left1
  Kraken23 = Kraken- Left1
  Kraken24 = Kraken- Left1
  Kraken25 = Kraken- Left1
  CANcoder11 = CTRE CANcoder [package=THT]
  CANrange1 = CTRE CANrange [package=THT]
  CANrange2 = CTRE CANrange [package=THT]
  R1 = Resistor [tolerance=±5% power=0.25W resistance=120 package=THT]

nets:
  N1: CANivore1.CANL[G], Pigeon_2_1.IN-CANH[Y]
  N2: CANivore1.CANH[Y], Pigeon_2_1.IN-CANL[G]
  N3: CANivore1.USB-C, cntl1.connector142
  N4: Kraken3.CAN_High_1, CANcoder3.OUT-CANH[Y]
  N5: Kraken3.CAN_Low_1, CANcoder3.OUT-CANL[G]
  N6: Kraken3.CAN_High_2, Kraken16.CAN_High_1
  N7: Kraken3.CAN_Low_2, Kraken16.CAN_Low_1
  N8: Kraken4.CAN_High_1, Kraken4.CAN_High_2, Kraken5.CAN_High_2, CANcoder3.IN-CANH[Y]
  N9: Kraken4.CAN_Low_1, Kraken4.CAN_Low_2, Kraken5.CAN_Low_2, CANcoder3.IN-CANL[G]
  N10: Kraken5.CAN_High_1, CANcoder4.OUT-CANH[Y]
  N11: Kraken5.CAN_Low_1, CANcoder4.OUT-CANL[G]
  N12: Kraken6.CAN_High_1, Kraken18.CAN_High_2
  N13: Kraken6.CAN_Low_1, Kraken18.CAN_Low_2
  N14: Kraken6.CAN_High_2, CANcoder4.IN-CANH[Y]
  N15: Kraken6.CAN_Low_2, CANcoder4.IN-CANL[G]
  N16: Pigeon_2_1.OUT-CANH[Y], CANcoder8.IN-CANL[G]
  N17: Pigeon_2_1.OUT-CANL[G], CANcoder8.IN-CANH[Y]
  N18: cntl1.connector41, RSL1.anode1
  N19: cntl1.connector42, RSL1.common_cathode
  N20: cntl1.connector138, RGB_Strip_LED30.Green_Connect
  N21: cntl1.connector144, switch4.RIO
  N22: switch4.AUX_1, J2.Ethernet
  N23: J2.USB-3, J3.pin1
  N24: J2.USB-4, J4.pin1
  N25: CANcoder7.IN-CANH[Y], CANcoder8.OUT-CANH[Y]
  N26: CANcoder7.IN-CANL[G], CANcoder8.OUT-CANL[G]
  N27: CANcoder7.OUT-CANH[Y], Kraken15.CAN_High_2
  N28: CANcoder7.OUT-CANL[G], Kraken15.CAN_Low_2
  N29: Kraken15.CAN_High_1, Kraken16.CAN_High_2
  N30: Kraken15.CAN_Low_1, Kraken16.CAN_Low_2
  N31: Kraken17.CAN_High_1, CANcoder10.OUT-CANH[Y]
  N32: Kraken17.CAN_Low_1, CANcoder10.OUT-CANL[G]
  N33: Kraken17.CAN_High_2, Kraken20.CAN_High_1
  N34: Kraken17.CAN_Low_2, Kraken20.CAN_Low_1
  N35: Kraken18.CAN_High_1, CANcoder9.+, CANcoder9.OUT-CANH[Y]
  N36: Kraken18.CAN_Low_1, CANcoder9.OUT-CANL[G]
  N37: Kraken19.CAN_High_1, Kraken23.CAN_High_2
  N38: Kraken19.CAN_Low_1, Kraken23.CAN_Low_2
  N39: Kraken19.CAN_High_2, CANcoder10.IN-CANH[Y]
  N40: Kraken19.CAN_Low_2, CANcoder10.IN-CANL[G]
  N41: Kraken20.CAN_High_2, CANcoder9.IN-CANH[Y]
  N42: Kraken20.CAN_Low_2, CANcoder9.IN-CANL[G]
  N43: Kraken22.CAN_High_1, CANcoder11.OUT-CANH[Y]
  N44: Kraken22.CAN_Low_1, CANcoder11.OUT-CANL[G], CANcoder11.-
  N45: Kraken22.CAN_High_2, Kraken24.CAN_High_1
  N46: Kraken22.CAN_Low_2, Kraken24.CAN_Low_1
  N47: Kraken23.CAN_High_1, Kraken24.CAN_High_2
  N48: Kraken23.CAN_Low_1, Kraken24.CAN_Low_2
  N49: Kraken25.CAN_High_1, CANrange1.CANH[Y], CANrange2.CANH[Y], R1.Pin_1
  N50: Kraken25.CAN_Low_1, CANrange1.CANL[G], CANrange2.CANL[G], R1.Pin_0
  N51: Kraken25.CAN_High_2, CANcoder11.IN-CANH[Y]
  N52: Kraken25.CAN_Low_2, CANcoder11.IN-CANL[G]

custom parts:
  Kraken- Left1: Kraken
  CTRE Pigeon 2.0: Generic single row SMD female header
  Generic female header - 5 pins: Generic female header
  FRC Robot Signal Light: Panel Mount Beacon,12V AC/DC,45 mm Panel Mounting LED,Amber,22.5 mm Round Mounting Hole Used as: R709 *ROBOTS must have a signal light. ROBOTS must use at least 1, but no more than 2, diagnostic ROBOT Signal Light (RSL) (P/N 855PB-B12ME522). Any RSL must be: A. mounted on the ROBOT such that it is easily visible while standing 3 ft. (~ 100 cm) in front of the ROBOT, B. connected to the “RSL”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
  Generic female header - 1 pins: Generic female header
  RGB Strip LED: A tri-color Strip LED with red, green and blue. Based on LED SMD 5050 RGB Pin order: common cathode - green - red - blue
