# Fritzing sketch 2025 Power Schematic (saved by Fritzing 1.0.2b)

parts:
  PDH1 = rev_pdh
  Kraken1 = Kraken-Right
  Kraken2 = Kraken-Right
  Kraken4 = Kraken-Right
  Kraken5 = Kraken-Right
  Kraken7 = Kraken- Left1
  Kraken8 = Kraken- Left1
  Kraken9 = Kraken- Left1
  F1 = Resettable Fuse PTC [package=0603]  # not connected
  F2 = Resettable Fuse PTC [package=0603]  # not connected
  F3 = Resettable Fuse PTC [package=0603]  # not connected
  F4 = Resettable Fuse PTC [package=0603]  # not connected
  F5 = Resettable Fuse PTC [package=0603]  # not connected
  F6 = Resettable Fuse PTC [package=0603]  # not connected
  F7 = Resettable Fuse PTC [package=0603]  # not connected
  F8 = Resettable Fuse PTC [package=0603]  # not connected
  CB1 = Thermal Circuit Breaker [package=waterproof]
  BAT1 = Battery 12V [package=battcom_20mm_pth]
  F9 = Resettable Fuse PTC [package=0603]  # not connected
  F10 = Resettable Fuse PTC [package=0603]  # not connected
  F11 = Resettable Fuse PTC [package=0603]  # not connected
  F12 = Resettable Fuse PTC [package=0603]  # not connected
  F13 = Resettable Fuse PTC [package=0603]  # not connected
  F14 = Resettable Fuse PTC [package=0603]  # not connected
  F15 = Resettable Fuse PTC [package=0603]  # not connected
  F16 = Resettable Fuse PTC [package=0603]  # not connected
  Kraken10 = Kraken- Left1
  Kraken13 = Kraken- Left1
  Kraken14 = Kraken-Right
  Kraken15 = Kraken-Right
  Kraken16 = Kraken-Right
  Kraken17 = Kraken-Right
  F17 = Resettable Fuse PTC [package=0603]  # not connected
  F18 = Resettable Fuse PTC [package=0603]  # not connected
  Kraken11 = Kraken- Left1
  F25 = Resettable Fuse PTC [package=0603]  # not connected
  F26 = Resettable Fuse PTC [package=0603]  # not connected
  JP2 = APP SB50 [package=sb50]
  JP3 = APP SB50 [package=sb50]
  Kraken6 = Kraken- Left1
  Kraken18 = Kraken-Right
  Mini_Power_Module1 = REV Mini Power Module [form="♀ (female)" package=THT]
  DC1 = Pololu reg29b 0J14085 Voltage Regulator
  J1 = Generic female header - 5 pins [form="♀ (female)" package=THT]
  switch1 = Network Switch
  cntl1 = roborio_v2
  Pigeon_2_1 = CTRE Pigeon 2.0 [package=THT]
  CANivore1 = CTRE CANivore [form="♀ (female)" package=THT]
  F27 = Resettable Fuse PTC [package=0603]  # not connected
  F28 = Resettable Fuse PTC [package=0603]  # not connected
  F29 = Resettable Fuse PTC [package=0603]  # not connected
  F30 = Resettable Fuse PTC [package=0603]  # not connected
  F31 = Resettable Fuse PTC [package=0603]  # not connected
  F32 = Resettable Fuse PTC [package=0603]  # not connected
  F33 = Resettable Fuse PTC [package=0603]  # not connected
  F34 = Resettable Fuse PTC [package=0603]  # not connected
  F35 = Resettable Fuse PTC [package=0603]  # not connected
  F36 = Resettable Fuse PTC [package=0603]  # not connected
  CANcoder1 = CTRE CANcoder [package=THT]
  CANrange1 = CTRE CANrange [package=THT]
  CANrange2 = CTRE CANrange [package=THT]
  CANcoder2 = CTRE CANcoder [package=THT]
  CANcoder3 = CTRE CANcoder [package=THT]
  CANcoder4 = CTRE CANcoder [package=THT]
  CANcoder5 = CTRE CANcoder [package=THT]
  CANcoder6 = CTRE CANcoder [package=THT]
  CANcoder7 = CTRE CANcoder [package=THT]
  RGB_Strip_LED32 = RGB Strip LED  # not connected
  RGB_Strip_LED33 = RGB Strip LED  # not connected
  RGB_Strip_LED37 = RGB Strip LED
  CANcoder8 = CTRE CANcoder [package=THT]
  CANcoder9 = CTRE CANcoder [package=THT]
  RGB_Strip_LED38 = RGB Strip LED
  RGB_Strip_LED40 = RGB Strip LED
  RGB_Strip_LED41 = RGB Strip LED  # not connected
  F37 = Resettable Fuse PTC [package=0603]  # not connected
  F38 = Resettable Fuse PTC [package=0603]  # not connected
  F39 = Resettable Fuse PTC [package=0603]  # not connected

nets:
  N1: PDH1.connector0, PDH1.connector4, Kraken4.+, Kraken14.+
  N2: PDH1.connector1, PDH1.connector5, Kraken4.-, Kraken14.-
  N3: PDH1.connector2, PDH1.connector6, Kraken5.+, Kraken15.+
  N4: PDH1.connector3, PDH1.connector7, Kraken5.-, Kraken15.-
  N5: PDH1.connector10, Kraken18.+
  N6: PDH1.connector11, Kraken18.-
  N7: PDH1.connector12, PDH1.connector16, Kraken2.+, Kraken17.+
  N8: PDH1.connector13, PDH1.connector17, Kraken2.-, Kraken17.-
  N9: PDH1.connector14, PDH1.connector18, Kraken1.+, Kraken16.+
  N10: PDH1.connector15, PDH1.connector19, Kraken1.-, Kraken16.-
  N11: PDH1.connector20, Kraken6.+
  N12: PDH1.connector21, Kraken6.-
  N13: PDH1.connector22, Kraken7.+
  N14: PDH1.connector23, Kraken7.-
  N15: PDH1.connector24, Mini_Power_Module1.Input_+
  N16: PDH1.connector25, Mini_Power_Module1.Input_-
  N17: PDH1.connector26, Kraken13.-
  N18: PDH1.connector27, Kraken13.+
  N19: PDH1.connector28, PDH1.connector36, Kraken9.-, Kraken11.-
  N20: PDH1.connector29, PDH1.connector37, Kraken9.+, Kraken11.+
  N21: PDH1.connector34, PDH1.connector38, Kraken8.-, Kraken10.-
  N22: PDH1.connector35, PDH1.connector39, Kraken8.+, Kraken10.+
  N23: PDH1.connector44, JP3.1
  N24: PDH1.connector45, CB1.1
  N25: PDH1.connector46, switch1.12v_+
  N26: PDH1.connector47, switch1.12v_-
  N27: PDH1.connector48, cntl1.connector39
  N28: PDH1.connector49, cntl1.connector40
  N29: PDH1.connector50, RGB_Strip_LED38.Blue_Connect
  N30: PDH1.connector51, RGB_Strip_LED38.Common_Connect
  N31: CB1.2, JP3.2
  N32: BAT1.+, JP2.2
  N33: BAT1.-, JP2.1
  N34: Mini_Power_Module1.5+, DC1.IN+
  N35: Mini_Power_Module1.5-, DC1.IN-
  N36: Mini_Power_Module1.4+, CANcoder2.+, CANcoder3.+
  N37: Mini_Power_Module1.4-, CANcoder2.-, CANcoder3.-
  N38: Mini_Power_Module1.3+, RGB_Strip_LED37.Common_Connect
  N39: Mini_Power_Module1.3-, RGB_Strip_LED37.Blue_Connect
  N40: Mini_Power_Module1.2+, CANcoder6.+, CANcoder6.IN-CANL[G], CANcoder6.OUT-CANH[Y], CANcoder7.+
  N41: Mini_Power_Module1.2-, CANcoder6.-, CANcoder7.-
  N42: Mini_Power_Module1.1+, CANcoder4.+, CANcoder5.+
  N43: Mini_Power_Module1.1-, CANcoder4.-, CANcoder5.-
  N44: Mini_Power_Module1.0+, Pigeon_2_1.+, CANivore1.V+[R]
  N45: Mini_Power_Module1.0-, Pigeon_2_1.-, CANivore1.V-[B]
  N46: DC1.OUT+, DC1.OUT-, J1.DC-Power_In
  N47: CANcoder1.+, CANrange1.-, CANrange2.-, RGB_Strip_LED40.Blue_Connect
  N48: CANcoder1.-, CANrange1.+, CANrange2.+, RGB_Strip_LED40.Common_Connect
  N49: CANcoder8.+, CANcoder9.+
  N50: CANcoder8.-, CANcoder9.-

custom parts:
  Kraken-Right: Kraken
  Kraken- Left1: Kraken
  Resettable Fuse PTC: Resettable Fuse PTC Resettable Fuse. Spark Fun Electronics SKU : COM-08357
  Thermal Circuit Breaker: Cooper Bussman P/N CB185-120, CB185F-120, CB285-120 CB285F-120, CB285120F or Optifuse P/N 153120, 253120
  Battery 12V: Battery Holders Various common sizes : AA, AAA, 20mm coin cell and 12mm coin cell.
  Resettable Fuse PTC: Resettable Fuse PTC Resettable Fuse. Spark Fun Electronics SKU : COM-08357
  Resettable Fuse PTC: Resettable Fuse PTC Resettable Fuse. Spark Fun Electronics SKU : COM-08357
  APP SB50: Anderson Power Products SB®50 Connectors feature a one-piece plastic housing using stainless steel springs to hold low-resistance contacts in place. These connectors work with wire contacts up to 6AWG (10mm²) as well as PCB and busbar contacts. The genderless design mates with itself and has a plated through-hole mounting style. Anderson SB®50 Connectors are UL-rated for hot plugging up to 50A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
  REV Mini Power Module: Generic female header
  Generic female header - 5 pins: Generic female header
  CTRE Pigeon 2.0: Generic single row SMD female header
  RGB Strip LED: A tri-color Strip LED with red, green and blue. Based on LED SMD 5050 RGB Pin order: common cathode - green - red - blue
